# Fritzing sketch Huskylens_Microbit_CameraCounter (saved by Fritzing 1.0.1rc)

parts:
  Mod1 = Microbit
  A1 = HuskyLens-Vision-Sensor_1
  BAT3 = 18650 battery holder [package=battery-18650-kit]
  D1 = Rectifier Diode [part_number=1N4001 package="Melf DO-213 AB [SMD]"]

nets:
  N1: Mod1.P19, A1.pin2
  N2: Mod1.P20, A1.pin1
  N3: Mod1.GND, Mod1.Bat_-, D1.anode
  N4: Mod1.Bat_+, A1.pin4, BAT3.-
  N5: A1.pin3, BAT3.+, D1.cathode

custom parts:
  Microbit: BBC Microbit Fritzing part. May 2019 expanded to include schematic and pcb views as well as breadboard. PCB view assumes an Adafruit PRODUCT ID: 3342 2x40 Right Angle through hole edge connector (although others will probably work as well). The pcb svg is custom (see forum article http://forum.fritzing.org/t/making-edge-connectors-and-both-side-smd-parts/7287 for an explaination if you need to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
  HuskyLens-Vision-Sensor_1: Huskylens is an easy-to-use AI Camera | Vision Sensor. DFrobot Huskylens is equipped with multiple functions, such as face recognition, object tracking, object recognition, line tracking, color recognition, and tag(QR code) recognition.
  18650 battery holder: 18650 Battery Holder identical to the dual battery version.
